// Logisim project №1 The basics.circ as structural Verilog: 1 circuit, main circuit main
module main (
  input  in_1,
  input  in_2,
  input  in_3,
  input  in_4,
  input  in_5,
  input  in_6,
  input  in_7,
  input  in_8,
  input  in_9,
  input  in_10,
  input  in_11,
  input  in_12,
  input  in_13,
  input  in_14,
  output \ИНВЕР ,
  output \БУФ ,
  output \ИЛИ_НЕ ,
  output \И ,
  output XOR,
  output \ИЛИ ,
  output \XOR_НЕ ,
  output \И_НЕ 
);

  not not_1 (\ИНВЕР , in_1);
  buf buffer_1 (\БУФ , in_3);
  and and_1 (\И , in_5, in_7);
  or or_1 (\ИЛИ , in_9, in_11);
  nand nand_1 (\И_НЕ , in_13, in_14);
  nor nor_1 (\ИЛИ_НЕ , in_2, in_4);
  xor xor_1 (XOR, in_6, in_8);
  xnor xnor_1 (\XOR_НЕ , in_10, in_12);
endmodule
