// Logisim project №2 XOR.circ as structural Verilog: 1 circuit, main circuit main
module main (
  input  in_1,
  input  in_2,
  input  in_3,
  input  in_4,
  output out_5,
  output out_6
);

  wire nand_1_out, or_1_out;

  xor xor_1 (out_5, in_1, in_2);
  or or_1 (or_1_out, in_3, in_4);
  nand nand_1 (nand_1_out, in_3, in_4);
  and and_1 (out_6, or_1_out, nand_1_out);

  // Notes on the sheet:
  //   XOR
endmodule
